// Logisim project cpu.circ as structural Verilog
module decompose (
  input  [31:0] in_1,
  output Suma,
  output Resta,
  output And,
  output Or,
  output Nor,
  output Beq,
  output AddI,
  output Load,
  output Store
);

  wire comparator_1_eq, comparator_2_eq, comparator_3_eq, comparator_4_eq, comparator_6_eq, comparator_7_eq,
       comparator_8_eq, comparator_9_eq, comparator_10_eq, not_1_out, not_2_out, not_3_out, not_4_out, Tipo_R;

  Comparator #(.width(6)) comparator_1 (.a(in_1[5:0]), .b(6'b100000), .eq(comparator_1_eq));  // open: gt, lt
  not not_1 (not_1_out, Tipo_R);
  Comparator #(.width(6)) comparator_2 (.a(in_1[31:26]), .b(6'b000100), .eq(comparator_2_eq));  // open: gt, lt
  and and_1 (Suma, Tipo_R, comparator_1_eq);
  and and_2 (Beq, not_1_out, comparator_2_eq);
  Comparator #(.width(6)) comparator_3 (.a(in_1[5:0]), .b(6'b100010), .eq(comparator_3_eq));  // open: gt, lt
  Comparator #(.width(6)) comparator_4 (.a(in_1[31:26]), .b(6'b001000), .eq(comparator_4_eq));  // open: gt, lt
  and and_3 (Resta, Tipo_R, comparator_3_eq);
  not not_2 (not_2_out, Tipo_R);
  and and_4 (AddI, not_2_out, comparator_4_eq);
  Comparator #(.width(6)) comparator_5 (.a(in_1[31:26]), .b({6{1'b0}}), .eq(Tipo_R));  // open: gt, lt
  Comparator #(.width(6)) comparator_6 (.a(in_1[5:0]), .b(6'b100100), .eq(comparator_6_eq));  // open: gt, lt
  and and_5 (And, Tipo_R, comparator_6_eq);
  not not_3 (not_3_out, Tipo_R);
  Comparator #(.width(6)) comparator_7 (.a(in_1[31:26]), .b(6'b100011), .eq(comparator_7_eq));  // open: gt, lt
  and and_6 (Load, not_3_out, comparator_7_eq);
  Comparator #(.width(6)) comparator_8 (.a(in_1[5:0]), .b(6'b100101), .eq(comparator_8_eq));  // open: gt, lt
  Comparator #(.width(6)) comparator_9 (.a(in_1[31:26]), .b(6'b101011), .eq(comparator_9_eq));  // open: gt, lt
  and and_7 (Or, Tipo_R, comparator_8_eq);
  not not_4 (not_4_out, Tipo_R);
  and and_8 (Store, not_4_out, comparator_9_eq);
  Comparator #(.width(6)) comparator_10 (.a(in_1[5:0]), .b(6'b100111), .eq(comparator_10_eq));  // open: gt, lt
  and and_9 (Nor, Tipo_R, comparator_10_eq);

  // Other names for the same wires on the sheet: Address[15:0] = in_1[15:0]; Funct[5:0] = in_1[5:0];
  //   Rd[4:0] = in_1[15:11]; Rt[4:0] = in_1[20:16]; Rs[4:0] = in_1[25:21]; OpCode[5:0] = in_1[31:26]
endmodule

module pc (
  input  clk,
  output [31:0] data
);

  wire [7:0] register_1_q_2;
  wire [23:0] register_1_q;
  wire [31:0] adder_1_out;

  Register #(.width(32)) register_1 (.D(adder_1_out), .Q({register_1_q_2, register_1_q}), .clk(clk));  // open: en, clr
  Adder #(.width(32)) adder_1 (.a(32'h1), .b({register_1_q_2, register_1_q}), .out(adder_1_out));  // open: cin, cout
  ROM rom_1 (.pos(register_1_q), .data(data));  // open: sel
endmodule

module RAM (
  input  [23:0] pos,
  input  [31:0] data,
  input  sel,
  input  clk,
  input  ld,
  input  clr
);

  RAM_part #(.addrWidth(24), .dataWidth(32)) ram_1 (.addr(pos), .data(data), .sel(sel), .clk(clk), .ld(ld), .clr(clr));
endmodule

module ROM (
  input  [23:0] pos,
  input  sel,
  output [31:0] data
);

  ROM_part #(.addrWidth(24), .dataWidth(32)) rom_1 (.addr(pos), .data(data), .sel(sel));
endmodule
